# Fritzing sketch anaconda (saved by Fritzing 0.6.3b)
breadboards: 1

parts:
  LCD1 = LCD screen
  Arduino1 = Arduino
  J1 = Piezo Speaker
  M1 = DC Motor
  T1 = LM35 Temperature Sensor [package="TO92 [THT]"]
  R1 = Photocell (LDR) [package=THT]
  IC1 = H-Bridge [package=THT]
  LED1 = LED - 5mm [color="Red (633nm)" package="5 mm [THT]"]

nets:
  GND: LCD1.VSS, LCD1.R/W, Arduino1.GND, J1.pin2, T1.GND, R1.pin_1, IC1.GND1, IC1.GND2, IC1.GND3, IC1.GND4, LED1.cathode
  VDD: LCD1.VDD, Arduino1.+5V, IC1.1_2EN, IC1.VCC2
  N1: LCD1.RS, Arduino1.D12
  N2: LCD1.E, Arduino1.D11
  N3: LCD1.DB4, Arduino1.D5
  N4: LCD1.DB5, Arduino1.D4
  N5: LCD1.DB6, Arduino1.D3
  N6: LCD1.DB7, Arduino1.D2
  N7: Arduino1.D13, J1.pin1
  N8: Arduino1.D10, IC1.1A
  N9: Arduino1.D9, IC1.2A
  N10: Arduino1.D0RX, LED1.anode
  N11: Arduino1.3V3, T1.+Vs
  N12: Arduino1.A0, T1.Vout
  N13: Arduino1.A1, R1.pin_0
  N14: M1.pin_1, IC1.1Y
  N15: M1.pin_2, IC1.2Y
  5V: IC1.VCC1
